// Logisim project ALU_1BIT_MSB.circ as structural Verilog: 1 circuit, main circuit main
module main (
  input  a,
  input  CarryIn,
  input  b,
  input  Binvert,
  input  Less,
  output Result,
  output Set
);

  wire adder_1_cout, and_1_out, multiplexer_1_out, not_1_out, or_1_out;

  Multiplexer multiplexer_1 (.in0(b), .in1(not_1_out), .out(multiplexer_1_out), .sel(Binvert));
  not not_1 (not_1_out, b);
  and and_1 (and_1_out, a, multiplexer_1_out);
  or or_1 (or_1_out, a, multiplexer_1_out);
  Adder #(.width(1)) adder_1 (.a(a), .b(multiplexer_1_out), .out(Set), .cin(CarryIn), .cout(adder_1_cout));
  Multiplexer #(.select(2)) multiplexer_2 (
    .in0(and_1_out), .in1(or_1_out), .in2(Set), .in3(Less), .out(Result));  // open: sel
endmodule
