// Logisim project HW_register_file.circ as structural Verilog: 1 circuit, main circuit main
module main (
  input  Write_register,
  input  Read_reigster1,
  input  [7:0] Write_data,
  input  Read_register2,
  input  Reg_Write,
  output [7:0] Read_data1,
  output [7:0] Read_data2
);

  wire and_1_out, and_2_out, clock_1_out, decoder_1_out0, decoder_1_out1;
  wire [7:0] Register0_q, Register1_q;

  Clock clock_1 (.out(clock_1_out));
  Decoder decoder_1 (.out0(decoder_1_out0), .out1(decoder_1_out1), .sel(Write_register), .en(1'b1));
  Register Register0 (.D(Write_data), .en(and_1_out), .clk(clock_1_out), .Q(Register0_q), .clr(1'b0));
  and and_1 (and_1_out, Reg_Write, decoder_1_out0);
  Register Register1 (.D(Write_data), .en(and_2_out), .clk(clock_1_out), .Q(Register1_q), .clr(1'b0));
  and and_2 (and_2_out, Reg_Write, decoder_1_out1);
  Multiplexer #(.width(8)) multiplexer_1 (.in0(Register0_q), .in1(Register1_q), .out(Read_data1), .sel(Read_reigster1));
  Multiplexer #(.width(8)) multiplexer_2 (.in0(Register0_q), .in1(Register1_q), .out(Read_data2), .sel(Read_register2));
endmodule
