// Logisim project Lab1_1212_counter.circ as structural Verilog: 2 circuits, main circuit main
module main (
  output [7:0] out_1
);

  wire clock_1_out;
  wire [7:0] register_1_q;

  Adder adder_1 (.a(8'h1), .b(register_1_q), .out(out_1));  // open: cin, cout
  Clock clock_1 (.out(clock_1_out));
  Register register_1 (.D(out_1), .clk(clock_1_out), .Q(register_1_q));  // open: en, clr
endmodule

module counterr (
  output [7:0] out_1
);

  wire clock_1_out;
  wire [7:0] register_1_q;

  Adder adder_1 (.a(8'h1), .b(register_1_q), .out(out_1));  // open: cin, cout
  Clock clock_1 (.out(clock_1_out));
  Register register_1 (.D(out_1), .clk(clock_1_out), .Q(register_1_q));  // open: en, clr
endmodule
