// Logisim project Lab1_1219_TruthTable.circ as structural Verilog: 4 circuits, main circuit main
module main (
  input  [5:0] in_1,
  output out_2,
  output out_3,
  output out_4,
  output out_5,
  output out_6,
  output out_7,
  output out_8,
  output [1:0] out_9
);

  Control control_1 (
    .Op(in_1), .RegDst(out_2), .ALUSrc(out_3), .MemtoReg(out_4), .RegWrite(out_5), .MemRead(out_6),
    .MemWrite(out_7), .Branch(out_8), .ALUOp(out_9));
endmodule

module FA (
  input  x,
  input  y,
  input  Cin,
  output S,
  output Cout
);

  wire and_1_out, and_2_out, and_3_out, and_4_out, and_5_out, and_6_out, and_7_out, not_1_out, not_2_out,
       not_3_out;

  not not_1 (not_1_out, x);
  not not_2 (not_2_out, y);
  not not_3 (not_3_out, Cin);
  and and_1 (and_1_out, not_1_out, not_2_out, Cin);
  and and_2 (and_2_out, not_1_out, y, not_3_out);
  and and_3 (and_3_out, x, not_2_out, not_3_out);
  and and_4 (and_4_out, x, y, Cin);
  and and_5 (and_5_out, y, Cin);
  and and_6 (and_6_out, x, Cin);
  and and_7 (and_7_out, x, y);
  or or_1 (S, and_1_out, and_2_out, and_3_out, and_4_out);
  or or_2 (Cout, and_5_out, and_6_out, and_7_out);
endmodule

module Control (
  input  [5:0] Op,
  output RegDst,
  output ALUSrc,
  output MemtoReg,
  output RegWrite,
  output MemRead,
  output MemWrite,
  output Branch,
  output [1:0] ALUOp
);

  wire not_1_out, not_2_out, not_3_out;

  not not_1 (not_1_out, Op[3]);
  not not_2 (not_2_out, Op[2]);
  not not_3 (not_3_out, Op[1]);
  and and_1 (RegDst, not_2_out, not_3_out);
  and and_2 (MemtoReg, not_1_out, Op[0]);
  and and_3 (RegWrite, not_1_out, not_2_out);
  and and_4 (MemRead, not_1_out, Op[0]);
  and and_5 (ALUOp[1], not_2_out, not_3_out);

  assign ALUOp[0] = Op[2];
  assign ALUSrc = Op[0];
  assign Branch = Op[2];
  assign MemWrite = Op[3];
endmodule

module second (
  input  [5:0] opcode,
  output RegDst,
  output ALUSrc,
  output MemtoReg,
  output Regwrite,
  output Memread,
  output MemWrite,
  output Branch,
  output [1:0] ALUOp1
);

  wire not_1_out, not_2_out;

  not not_1 (not_1_out, opcode[3]);
  not not_2 (not_2_out, opcode[2]);
  not not_3 (RegDst, opcode[1]);
  and and_1 (Regwrite, not_1_out, not_2_out);
  and and_2 (Memread, not_1_out, opcode[0]);
  and and_3 (ALUOp1[1], not_2_out, RegDst);

  assign ALUOp1[0] = opcode[2];
  assign ALUSrc = opcode[0];
  assign Branch = opcode[2];
  assign MemtoReg = opcode[0];
  assign MemWrite = opcode[3];
endmodule
