// Logisim project Lab2_1205_8-bit_ALU.circ as structural Verilog: 3 circuits, main circuit MST_1bit_ALU
module MST_1bit_ALU (
  input  a,
  input  CarryIn,
  input  b,
  input  Binvert,
  input  Less,
  input  [1:0] Operation,
  output Result,
  output Set,
  output CarryOut
);

  wire and_1_out, multiplexer_1_out, not_1_out, or_1_out;

  Multiplexer multiplexer_1 (.in0(b), .in1(not_1_out), .out(multiplexer_1_out), .sel(Binvert));
  not not_1 (not_1_out, b);
  and and_1 (and_1_out, a, multiplexer_1_out);
  or or_1 (or_1_out, a, multiplexer_1_out);
  Adder #(.width(1)) adder_1 (.a(a), .b(multiplexer_1_out), .out(Set), .cin(CarryIn), .cout(CarryOut));
  Multiplexer #(.select(2)) multiplexer_2 (
    .in0(and_1_out), .in1(or_1_out), .in2(Set), .in3(Less), .out(Result), .sel(Operation));
endmodule

module ALU_1bit (
  input  a,
  input  b,
  input  CarryIn,
  input  Binvert,
  input  Less,
  input  [1:0] Operation,
  output Result,
  output CarryOut
);

  wire adder_1_out, and_1_out, multiplexer_1_out, not_1_out, or_1_out;

  not not_1 (not_1_out, b);
  Multiplexer multiplexer_1 (.in0(b), .in1(not_1_out), .out(multiplexer_1_out), .sel(Binvert));
  and and_1 (and_1_out, a, multiplexer_1_out);
  or or_1 (or_1_out, a, multiplexer_1_out);
  Adder #(.width(1)) adder_1 (.a(a), .b(multiplexer_1_out), .out(adder_1_out), .cin(CarryIn), .cout(CarryOut));
  Multiplexer #(.select(2)) multiplexer_2 (
    .in0(and_1_out), .in1(or_1_out), .in2(adder_1_out), .in3(Less), .out(Result), .sel(Operation));
endmodule

module main (
  input  CarryIn,
  input  [1:0] Operations,
  input  Binvert,
  input  [7:0] a,
  input  [7:0] b,
  output [7:0] Result,
  output CarryOut
);

  wire alu_1bit_1_carryout, alu_1bit_2_carryout, alu_1bit_3_carryout, alu_1bit_4_carryout,
       alu_1bit_5_carryout, alu_1bit_6_carryout, alu_1bit_7_carryout, mst_1bit_alu_1_set;

  ALU_1bit alu_1bit_1 (
    .a(a[0]), .b(b[0]), .CarryIn(CarryIn), .Binvert(Binvert), .Less(mst_1bit_alu_1_set),
    .Operation(Operations), .Result(Result[0]), .CarryOut(alu_1bit_1_carryout));
  ALU_1bit alu_1bit_2 (
    .a(a[1]), .b(b[1]), .CarryIn(alu_1bit_1_carryout), .Binvert(Binvert), .Less(1'b0),
    .Operation(Operations), .Result(Result[1]), .CarryOut(alu_1bit_2_carryout));
  ALU_1bit alu_1bit_3 (
    .a(a[2]), .b(b[2]), .CarryIn(alu_1bit_2_carryout), .Binvert(Binvert), .Less(1'b0),
    .Operation(Operations), .Result(Result[2]), .CarryOut(alu_1bit_3_carryout));
  ALU_1bit alu_1bit_4 (
    .a(a[3]), .b(b[3]), .CarryIn(alu_1bit_3_carryout), .Binvert(Binvert), .Less(1'b0),
    .Operation(Operations), .Result(Result[3]), .CarryOut(alu_1bit_4_carryout));
  ALU_1bit alu_1bit_5 (
    .a(a[4]), .b(b[4]), .CarryIn(alu_1bit_4_carryout), .Binvert(Binvert), .Less(1'b0),
    .Operation(Operations), .Result(Result[4]), .CarryOut(alu_1bit_5_carryout));
  ALU_1bit alu_1bit_6 (
    .a(a[5]), .b(b[5]), .CarryIn(alu_1bit_5_carryout), .Binvert(Binvert), .Less(1'b0),
    .Operation(Operations), .Result(Result[5]), .CarryOut(alu_1bit_6_carryout));
  ALU_1bit alu_1bit_7 (
    .a(a[6]), .b(b[6]), .CarryIn(alu_1bit_6_carryout), .Binvert(Binvert), .Less(1'b0),
    .Operation(Operations), .Result(Result[6]), .CarryOut(alu_1bit_7_carryout));
  MST_1bit_ALU mst_1bit_alu_1 (
    .a(a[7]), .CarryIn(alu_1bit_7_carryout), .b(b[7]), .Binvert(Binvert), .Less(1'b0),
    .Operation(Operations), .Result(Result[7]), .Set(mst_1bit_alu_1_set), .CarryOut(CarryOut));
endmodule
