// Logisim project Lab2_1212_RAM.circ as structural Verilog: 3 circuits, main circuit main
module main (
  input  in_1,
  input  in_2,
  input  in_3,
  input  [7:0] in_4,
  output [7:0] out_5
);

  wire clock_1_out;
  wire [7:0] adder_1_out, PC_q;

  Clock clock_1 (.out(clock_1_out));
  Register PC (.D(adder_1_out), .en(in_1), .clk(clock_1_out), .Q(PC_q));  // open: clr
  Adder adder_1 (.a(8'h1), .b(PC_q), .out(adder_1_out));  // open: cin, cout
  RAM ram_1 (.addr(PC_q), .we(in_2), .oe(in_3), .clk(clock_1_out), .din(in_4), .dout(out_5));
endmodule

module RAMM (
  input  [7:0] in_1,
  input  in_2,
  input  in_3,
  input  [7:0] in_4,
  output [7:0] out_5
);

  wire clock_1_out;

  Clock clock_1 (.out(clock_1_out));
  RAM ram_1 (.addr(in_1), .we(in_2), .oe(in_3), .clk(clock_1_out), .din(in_4), .dout(out_5));
endmodule

module counterr (
  output [7:0] out_1
);

  wire clock_1_out;
  wire [7:0] register_1_q;

  Adder adder_1 (.a(8'h1), .b(register_1_q), .out(out_1));  // open: cin, cout
  Clock clock_1 (.out(clock_1_out));
  Register register_1 (.D(out_1), .clk(clock_1_out), .Q(register_1_q));  // open: en, clr
endmodule
