// Logisim project cpu.circ as structural Verilog: 7 circuits, main circuit Register_File
module main (
);

  wire alu_8bits_1_zero, and_1_out, clock_1_out, control_1_binvert, control_1_branch, control_1_regorimm,
       control_1_regormem, control_1_regwrite, multiplexer_2_out, multiplexer_3_out, multiplexer_4_out;
  wire [1:0] control_1_operation;
  wire [4:0] rom_1_data_2;
  wire [4:2] rom_1_data;
  wire [7:0] adder_1_out, adder_2_out, alu_8bits_1_result, bit_extender_1_out, bit_extender_2_out,
       multiplexer_1_out, multiplexer_5_out, multiplexer_6_out, PC_q, register_file_1_read_data1,
       register_file_1_read_data2, rom_2_data;

  Clock clock_1 (.out(clock_1_out));
  Register PC (.D(multiplexer_1_out), .en(1'b1), .clk(clock_1_out), .Q(PC_q));  // open: clr
  Adder adder_1 (.a(8'h1), .b(PC_q), .out(adder_1_out));  // open: cin, cout
  assign bit_extender_1_out = {{3{rom_1_data[4]}}, {rom_1_data, rom_1_data[3:2]}};  // Bit_Extender bit_extender_1
  Adder adder_2 (.a(adder_1_out), .b(bit_extender_1_out), .out(adder_2_out));  // open: cin, cout
  ROM rom_1 (.addr(PC_q), .data({rom_1_data_2[4:2], rom_1_data, rom_1_data_2[1:0]}));
  Multiplexer #(.width(8)) multiplexer_1 (
    .in0(adder_1_out), .in1(adder_2_out), .out(multiplexer_1_out), .sel(and_1_out));
  and and_1 (and_1_out, alu_8bits_1_zero, control_1_branch);
  assign bit_extender_2_out = {{4{1'b0}}, {rom_1_data[3:2], rom_1_data[3:2]}};  // Bit_Extender bit_extender_2
  Multiplexer multiplexer_2 (
    .in0(rom_1_data[3]), .in1(rom_1_data[4]), .out(multiplexer_2_out), .sel(control_1_regorimm));
  Control control_1 (
    .OP(rom_1_data_2), .RegWrite(control_1_regwrite), .Operation(control_1_operation),
    .BinVert(control_1_binvert), .RegOrMem(control_1_regormem), .RegOrImm(control_1_regorimm),
    .Branch(control_1_branch));
  Multiplexer multiplexer_3 (.in0(multiplexer_2_out), .in1(1'b1), .out(multiplexer_3_out), .sel(control_1_branch));
  Multiplexer multiplexer_4 (.in0(rom_1_data[2]), .in1(1'b0), .out(multiplexer_4_out), .sel(control_1_branch));
  Multiplexer #(.width(8)) multiplexer_5 (
    .in0(alu_8bits_1_result), .in1(rom_2_data), .out(multiplexer_5_out), .sel(control_1_regormem));
  Register_File register_file_1 (
    .Read_reigster1(multiplexer_3_out), .Read_register2(multiplexer_4_out), .Write_register(rom_1_data[4]),
    .Write_data(multiplexer_5_out), .CLK(clock_1_out), .Reg_Write(control_1_regwrite),
    .Read_data1(register_file_1_read_data1), .Read_data2(register_file_1_read_data2));
  Multiplexer #(.width(8)) multiplexer_6 (
    .in0(register_file_1_read_data2), .in1(bit_extender_2_out), .out(multiplexer_6_out),
    .sel(control_1_regorimm));
  ALU_8bits alu_8bits_1 (
    .Operations(control_1_operation), .CarryIn(control_1_binvert), .Binvert(control_1_binvert),
    .a(register_file_1_read_data1), .b(multiplexer_6_out), .Result(alu_8bits_1_result),
    .Zero(alu_8bits_1_zero));  // open: CarryOut
  ROM rom_2 (.addr(bit_extender_2_out), .data(rom_2_data));

  // Notes on the sheet:
  //   contents of rom_1 (hex, n*v repeats v):
  //   0 3b 25 50 fd af
  //   R-type + lw + ori + beq with control
  //   指令:          machine code:          結果:
  //   nop                          00                     nop
  //   sub $1, $1, $0           3b                     $1=2
  //   or  $0, $0, $1          25                    $0 = 3
  //   lw  $1, 0                  50                      $1 = 0
  //   beq -3                    fd                      $pc =$pc+1
  //   ori $0, f                    af                    $0 = 00
  //   beq -3                    fd                      $pc =6
  //   add $1, $1, $0            3a                 $1 = 3
  //   add $0, $0, $1        31                   $0 = 11
  //   lw  $1, 4                     54                     $1 = 11
  //   nop                      00                       nop
  //   sub $0, $0, $0           38                         $0 = 0
  //   暫存器預設值: $0 = 1, $1 = 3        Data Mem[3] = ff, Data Mem[4] = 11
  //   姓名:莊昕珉      學號:111321029
  //   Branch
  //   ori
  //   Branch:
  //   add $0, $0, $1        31                   $0 = 22
  //   lw  $1, 4                     54                     $1 = 11
  //   Branch1
  //   Branch2
  //   RegOrMem
  //   RegOrImm
  //   contents of rom_2 (hex, n*v repeats v):
  //   0 0 0 ff 11
endmodule

module Register_File (
  input  Read_reigster1,
  input  Read_register2,
  input  Write_register,
  input  [7:0] Write_data,
  input  CLK,
  input  Reg_Write,
  output [7:0] Read_data1,
  output [7:0] Read_data2
);

  wire and_1_out, and_2_out, decoder_1_out0, decoder_1_out1;
  wire [7:0] Register0_q, Register1_q;

  Decoder decoder_1 (.out0(decoder_1_out0), .out1(decoder_1_out1), .sel(Write_register), .en(1'b1));
  Register Register0 (.D(Write_data), .en(and_1_out), .clk(CLK), .Q(Register0_q), .clr(1'b0));
  and and_1 (and_1_out, Reg_Write, decoder_1_out0);
  Register Register1 (.D(Write_data), .en(and_2_out), .clk(CLK), .Q(Register1_q), .clr(1'b0));
  and and_2 (and_2_out, Reg_Write, decoder_1_out1);
  Multiplexer #(.width(8)) multiplexer_1 (.in0(Register0_q), .in1(Register1_q), .out(Read_data1), .sel(Read_reigster1));
  Multiplexer #(.width(8)) multiplexer_2 (.in0(Register0_q), .in1(Register1_q), .out(Read_data2), .sel(Read_register2));
endmodule

module MST_1bit_ALU (
  input  a,
  input  CarryIn,
  input  b,
  input  Binvert,
  input  Less,
  input  [1:0] Operation,
  output Result,
  output Set,
  output CarryOut
);

  wire and_1_out, multiplexer_1_out, not_1_out, or_1_out;

  Multiplexer multiplexer_1 (.in0(b), .in1(not_1_out), .out(multiplexer_1_out), .sel(Binvert));
  not not_1 (not_1_out, b);
  and and_1 (and_1_out, a, multiplexer_1_out);
  or or_1 (or_1_out, a, multiplexer_1_out);
  Adder #(.width(1)) adder_1 (.a(a), .b(multiplexer_1_out), .out(Set), .cin(CarryIn), .cout(CarryOut));
  Multiplexer #(.select(2)) multiplexer_2 (
    .in0(and_1_out), .in1(or_1_out), .in2(Set), .in3(Less), .out(Result), .sel(Operation));
endmodule

module ALU_1bit (
  input  a,
  input  b,
  input  CarryIn,
  input  Binvert,
  input  Less,
  input  [1:0] Operation,
  output Result,
  output CarryOut
);

  wire adder_1_out, and_1_out, multiplexer_1_out, not_1_out, or_1_out;

  not not_1 (not_1_out, b);
  Multiplexer multiplexer_1 (.in0(b), .in1(not_1_out), .out(multiplexer_1_out), .sel(Binvert));
  and and_1 (and_1_out, a, multiplexer_1_out);
  or or_1 (or_1_out, a, multiplexer_1_out);
  Adder #(.width(1)) adder_1 (.a(a), .b(multiplexer_1_out), .out(adder_1_out), .cin(CarryIn), .cout(CarryOut));
  Multiplexer #(.select(2)) multiplexer_2 (
    .in0(and_1_out), .in1(or_1_out), .in2(adder_1_out), .in3(Less), .out(Result), .sel(Operation));
endmodule

module ALU_8bits (
  input  [1:0] Operations,
  input  CarryIn,
  input  Binvert,
  input  [7:0] a,
  input  [7:0] b,
  output [7:0] Result,
  output CarryOut,
  output Zero
);

  wire alu_1bit_1_carryout, alu_1bit_2_carryout, alu_1bit_3_carryout, alu_1bit_4_carryout,
       alu_1bit_5_carryout, alu_1bit_6_carryout, alu_1bit_7_carryout, mst_1bit_alu_1_set, or_1_out;

  ALU_1bit alu_1bit_1 (
    .a(a[0]), .b(b[0]), .CarryIn(CarryIn), .Binvert(Binvert), .Less(mst_1bit_alu_1_set),
    .Operation(Operations), .Result(Result[0]), .CarryOut(alu_1bit_1_carryout));
  ALU_1bit alu_1bit_2 (
    .a(a[1]), .b(b[1]), .CarryIn(alu_1bit_1_carryout), .Binvert(Binvert), .Less(1'b0),
    .Operation(Operations), .Result(Result[1]), .CarryOut(alu_1bit_2_carryout));
  ALU_1bit alu_1bit_3 (
    .a(a[2]), .b(b[2]), .CarryIn(alu_1bit_2_carryout), .Binvert(Binvert), .Less(1'b0),
    .Operation(Operations), .Result(Result[2]), .CarryOut(alu_1bit_3_carryout));
  ALU_1bit alu_1bit_4 (
    .a(a[3]), .b(b[3]), .CarryIn(alu_1bit_3_carryout), .Binvert(Binvert), .Less(1'b0),
    .Operation(Operations), .Result(Result[3]), .CarryOut(alu_1bit_4_carryout));
  ALU_1bit alu_1bit_5 (
    .a(a[4]), .b(b[4]), .CarryIn(alu_1bit_4_carryout), .Binvert(Binvert), .Less(1'b0),
    .Operation(Operations), .Result(Result[4]), .CarryOut(alu_1bit_5_carryout));
  ALU_1bit alu_1bit_6 (
    .a(a[5]), .b(b[5]), .CarryIn(alu_1bit_5_carryout), .Binvert(Binvert), .Less(1'b0),
    .Operation(Operations), .Result(Result[5]), .CarryOut(alu_1bit_6_carryout));
  ALU_1bit alu_1bit_7 (
    .a(a[6]), .b(b[6]), .CarryIn(alu_1bit_6_carryout), .Binvert(Binvert), .Less(1'b0),
    .Operation(Operations), .Result(Result[6]), .CarryOut(alu_1bit_7_carryout));
  MST_1bit_ALU mst_1bit_alu_1 (
    .a(a[7]), .CarryIn(alu_1bit_7_carryout), .b(b[7]), .Binvert(Binvert), .Less(1'b0),
    .Operation(Operations), .Result(Result[7]), .Set(mst_1bit_alu_1_set), .CarryOut(CarryOut));
  or or_1 (or_1_out, Result[0], Result[1], Result[2], Result[3], Result[4], Result[5], Result[6], Result[7]);
  not not_1 (Zero, or_1_out);
endmodule

module counterr (
  output [7:0] out_1
);

  wire clock_1_out;
  wire [7:0] register_1_q;

  Adder adder_1 (.a(8'h1), .b(register_1_q), .out(out_1));  // open: cin, cout
  Clock clock_1 (.out(clock_1_out));
  Register register_1 (.D(out_1), .clk(clock_1_out), .Q(register_1_q));  // open: en, clr
endmodule

module Control (
  input  [4:0] OP,
  output RegWrite,
  output [1:0] Operation,
  output BinVert,
  output RegOrMem,
  output RegOrImm,
  output Branch
);

  wire and_1_out, and_2_out, and_3_out, and_4_out, and_5_out, and_6_out, not_1_out, not_2_out, not_4_out;

  not not_1 (not_1_out, OP[4]);
  not not_2 (not_2_out, OP[3]);
  not not_3 (RegOrMem, OP[2]);
  not not_4 (not_4_out, OP[1]);
  and and_1 (and_1_out, not_2_out, OP[2]);
  and and_2 (and_2_out, OP[3], RegOrMem);
  and and_3 (and_3_out, not_1_out, OP[1]);
  and and_4 (and_4_out, OP[4], not_2_out);
  and and_5 (and_5_out, not_2_out, not_4_out, OP[0]);
  and and_6 (and_6_out, not_1_out, OP[1], OP[0]);
  and and_7 (RegOrImm, OP[4], not_2_out);
  and and_8 (Branch, OP[4], OP[3]);
  or or_1 (RegWrite, and_1_out, and_2_out);
  or or_2 (Operation[1], and_3_out, OP[3]);
  or or_3 (Operation[0], and_4_out, and_5_out);
  or or_4 (BinVert, and_6_out, OP[3]);
endmodule
